// Logisim project 4.Bit.Adder.circ as structural Verilog: 2 circuits, main circuit main
module main (
  input  [3:0] A,
  input  C_in,
  input  [3:0] B,
  output [3:0] S_out,
  output C_out
);

  wire n1_bit_adder_1_c_out, n1_bit_adder_2_c_out, n1_bit_adder_3_c_out;

  _1_Bit_Adder u_1_bit_adder_1 (.A(A[0]), .B(B[0]), .C_in(C_in), .S(S_out[0]), .C_out(n1_bit_adder_1_c_out));
  _1_Bit_Adder u_1_bit_adder_2 (
    .A(A[1]), .B(B[1]), .C_in(n1_bit_adder_1_c_out), .S(S_out[1]), .C_out(n1_bit_adder_2_c_out));
  _1_Bit_Adder u_1_bit_adder_3 (
    .A(A[2]), .B(B[2]), .C_in(n1_bit_adder_2_c_out), .S(S_out[2]), .C_out(n1_bit_adder_3_c_out));
  _1_Bit_Adder u_1_bit_adder_4 (.A(A[3]), .B(B[3]), .C_in(n1_bit_adder_3_c_out), .S(S_out[3]), .C_out(C_out));
endmodule

module _1_Bit_Adder (
  input  A,
  input  B,
  input  C_in,
  output S,
  output C_out
);

  wire and_1_out, and_2_out, xor_1_out;

  xor xor_1 (xor_1_out, A, B);
  xor xor_2 (S, xor_1_out, C_in);
  and and_1 (and_1_out, xor_1_out, C_in);
  and and_2 (and_2_out, A, B);
  or or_1 (C_out, and_1_out, and_2_out);
endmodule
