// Logisim project 8.Bit.Adder.circ as structural Verilog: 1 circuit, main circuit main
module main (
  input  [7:0] A,
  input  in_2,
  input  [7:0] B,
  output out_4
);

  wire main_1_p5;
  wire [3:0] main_1_p1;
  wire [7:4] main_2_p1;

  // _4_Bit_Adder_main main_1: pin names not known; wires that end beside it: main_1_p1, A[3:0], in_2, B[3:0], main_1_p5
  // Probe on {main_2_p1, main_1_p1}
  // _4_Bit_Adder_main main_2: pin names not known; wires that end beside it: main_2_p1, A[7:4], main_1_p5, B[7:4], out_4
endmodule
