// Logisim project MIPS32-Update-4.circ as structural Verilog: 35 circuits, main circuit MIPS32
module MIPS32 (
);

  wire and_1_out, Branch_Logic_branch_jump_bool, Branch_Logic_isbranch, clock_1_out, EX_MEM_i_2,
       EX_MEM_movbit_2, EX_MEM_r_2, EX_MEM_we_2, Forward_Unit_m_to_ex_forward_a,
       Forward_Unit_m_to_ex_forward_b, Forward_Unit_w_to_ex_forward_a, Forward_Unit_w_to_ex_forward_b,
       I_Decode_usecomparator, I_q, islink_2_q, islink_q, isreg_q, JAL_out, JALR_out, JUMP_decode_isjump,
       JUMP_decode_islink, JUMP_decode_isregjump, LOAD_STORE_CONTROL_BITS_2_byte_2,
       LOAD_STORE_CONTROL_BITS_2_load_2, LOAD_STORE_CONTROL_BITS_2_store_2,
       LOAD_STORE_CONTROL_BITS_2_unsigned_2, LOAD_STORE_CONTROL_BITS_2_word_2,
       LOAD_STORE_CONTROL_BITS_byte_2, LOAD_STORE_CONTROL_BITS_load_2, LOAD_STORE_CONTROL_BITS_store_2,
       LOAD_STORE_CONTROL_BITS_unsigned_2, LOAD_STORE_CONTROL_BITS_word_2, LOAD_STORE_DECODE_byte,
       LOAD_STORE_DECODE_load, LOAD_STORE_DECODE_store, LOAD_STORE_DECODE_unsigned, LOAD_STORE_DECODE_word,
       MOVbit_q, MOVSelector_mov_we, multiplexer_5_out, multiplexer_7_out, NO_MOV_out,
       nonboolbranch_1_isbranchtype, or_1_out, or_2_out, R_Decode_movbit, R_Decode_usecomparator, R_q,
       registerfile_1_p3, stall_unit_stall, Type_Detector_i, Type_Detector_r, Type_Detector_we,
       USECOMPARATOR_q, WE_q;
  wire [3:0] BYTE_decoder_byte, I_Decode_aluop, ID_EX_aluop_2, multiplexer_4_out, multiplexer_17_out,
       multiplexer_18_out, R_Decode_aluop;
  wire [4:0] EX_MEM_rd_2, I_Decode_rd, ID_EX_rd_2, ID_EX_shamt_2, multiplexer_6_out, multiplexer_8_out,
       R_Decode_ra, R_Decode_rb, R_Decode_rd, R_Decode_shamt, ra_q, rb_q, registerfile_1_p4,
       SHAMT_ALTER_shamt_2;
  wire [5:0] EX_MEM_op_2, Func_q, ID_EX_op_2, R_Decode_func, R_Decode_opcode;
  wire [19:0] BYTE_decoder_target_2;
  wire [31:0] Branch_Logic_out_7, Comparator_result, EX_MEM_b_first_2, EX_MEM_result_2, EX_MEM_valb_2,
       I_Decode_immediate, ID_EX_immediate_2, ID_EX_pc_2, ID_EX_ra_2, ID_EX_rb_2,
       IF_ID_Pipeline_Register_instruction_2, IF_ID_Pipeline_Register_pc_4_2, mips_alu_1_p5, mips_ram_1_p7,
       mipsprogramrom_1_p3, MOVSelector_result, multiplexer_1_out, multiplexer_2_out, multiplexer_3_out,
       multiplexer_9_out, multiplexer_10_out, multiplexer_11_out, multiplexer_12_out, multiplexer_13_out,
       multiplexer_14_out, multiplexer_15_out, multiplexer_16_out, multiplexer_19_out, PC_2_q, PC___4_pc_4,
       PC_q, registerfile_1_p1, registerfile_1_p7, registerfile_1_p8;

  PC_4 PC___4 (.PCin(PC_q), .PC_4(PC___4_pc_4));
  // Probe on registerfile_1_p7
  // Probe on Branch_Logic_out_7
  Multiplexer #(.width(32)) multiplexer_1 (
    .in0(PC___4_pc_4), .in1(Branch_Logic_out_7), .out(multiplexer_1_out), .sel(Branch_Logic_branch_jump_bool));  // open: en
  Multiplexer #(.width(32)) multiplexer_2 (
    .in0(multiplexer_3_out), .in1(IF_ID_Pipeline_Register_pc_4_2), .out(multiplexer_2_out),
    .sel(stall_unit_stall));  // open: en
  Multiplexer #(.width(32)) multiplexer_3 (
    .in0(multiplexer_1_out), .in1(registerfile_1_p7), .out(multiplexer_3_out), .sel(JUMP_decode_isregjump));  // open: en
  Register #(.width(32)) PC (.D(multiplexer_2_out), .Q(PC_q), .clk(clock_1_out));  // open: en, clr
  // NOT_Gate not_1 has open pins: in=stall_unit_stall, out=open
  Clock clock_1 (.out(clock_1_out));
  // MIPSProgramROM mipsprogramrom_1: pin names not known; wires that end beside it: PC_q, multiplexer_3_out, mipsprogramrom_1_p3
  // Probe on IF_ID_Pipeline_Register_pc_4_2
  IF_ID_Pipeline_Register IF_ID_Pipeline_Register (
    .Instruction(mipsprogramrom_1_p3), .PC_4(multiplexer_2_out), .Clock(clock_1_out),
    .Instruction_2(IF_ID_Pipeline_Register_instruction_2), .PC_4_2(IF_ID_Pipeline_Register_pc_4_2));
  stall_unit stall_unit (
    .ID_EX_MEMREAD(or_1_out), .IF_ID_RA(R_Decode_ra), .ID_EX_rd(ID_EX_rd_2), .IF_ID_RB(R_Decode_rb),
    .STALL(stall_unit_stall));
  R_Everything R_Decode (
    .Instruction(IF_ID_Pipeline_Register_instruction_2), .Func(R_Decode_func), .movbit(R_Decode_movbit),
    .ALUop(R_Decode_aluop), .USECOMPARATOR(R_Decode_usecomparator), .shamt(R_Decode_shamt), .rd(R_Decode_rd),
    .rb(R_Decode_rb), .ra(R_Decode_ra), .opcode(R_Decode_opcode));
  Ins_Type_Decoder Type_Detector (
    .Instruction(IF_ID_Pipeline_Register_instruction_2), .R(Type_Detector_r), .I(Type_Detector_i),
    .WE(Type_Detector_we));
  // Probe on R_Decode_opcode
  JUMP_DECODE JUMP_decode (
    .INSTR(IF_ID_Pipeline_Register_instruction_2), .IsRegJump(JUMP_decode_isregjump),
    .IsLink(JUMP_decode_islink), .IsJump(JUMP_decode_isjump));
  NonBoolBranch nonboolbranch_1 (
    .INSTR(IF_ID_Pipeline_Register_instruction_2), .IsBranchType(nonboolbranch_1_isbranchtype));
  // Probe on registerfile_1_p1
  I_Everything I_Decode (
    .in_1(IF_ID_Pipeline_Register_instruction_2), .immediate(I_Decode_immediate), .rd(I_Decode_rd),
    .ALUop(I_Decode_aluop), .useCOMPARATOR(I_Decode_usecomparator));  // open: rs
  PC_BRANCH_HARDWARE Branch_Logic (
    .PC(IF_ID_Pipeline_Register_pc_4_2), .Immediate(I_Decode_immediate), .A(registerfile_1_p7),
    .B(registerfile_1_p8), .INSTR(IF_ID_Pipeline_Register_instruction_2), .IsJump(JUMP_decode_isjump),
    .out_7(Branch_Logic_out_7), .Branch_Jump_Bool(Branch_Logic_branch_jump_bool),
    .IsBranch(Branch_Logic_isbranch));
  // Probe on registerfile_1_p4
  Multiplexer #(.width(4)) multiplexer_4 (
    .in0(I_Decode_aluop), .in1(R_Decode_aluop), .out(multiplexer_4_out), .sel(Type_Detector_r));  // open: en
  // RegisterFile registerfile_1: pin names not known; wires that end beside it: registerfile_1_p1, clock_1_out, registerfile_1_p3, registerfile_1_p4, R_Decode_ra, R_Decode_rb, registerfile_1_p7, registerfile_1_p8
  Multiplexer #(.enable("false")) multiplexer_5 (
    .in0(I_Decode_usecomparator), .in1(R_Decode_usecomparator), .out(multiplexer_5_out), .sel(Type_Detector_r));
  LOAD_STORE_HARDWARE LOAD_STORE_DECODE (
    .in_1(R_Decode_opcode), .BYTE(LOAD_STORE_DECODE_byte), .WORD(LOAD_STORE_DECODE_word),
    .Unsigned(LOAD_STORE_DECODE_unsigned), .Load(LOAD_STORE_DECODE_load), .Store(LOAD_STORE_DECODE_store));
  or or_1 (or_1_out, LOAD_STORE_CONTROL_BITS_load_2, nonboolbranch_1_isbranchtype);
  Multiplexer #(.width(5)) multiplexer_6 (
    .in0(I_Decode_rd), .in1(R_Decode_rd), .out(multiplexer_6_out), .sel(Type_Detector_r));  // open: en
  Multiplexer multiplexer_7 (
    .in0(LOAD_STORE_DECODE_load), .in1(1'b0), .out(multiplexer_7_out), .sel(stall_unit_stall));  // open: en
  SHAMT_Decoder SHAMT_ALTER (
    .OpCode(R_Decode_opcode), .Shamt(R_Decode_shamt), .Func(R_Decode_func), .A(registerfile_1_p7),
    .SHAMT_2(SHAMT_ALTER_shamt_2));
  Multiplexer #(.width(5)) multiplexer_8 (
    .in0(multiplexer_6_out), .in1({5{1'b1}}), .out(multiplexer_8_out), .sel(JUMP_decode_islink));  // open: en
  and and_1 (and_1_out, R_Decode_movbit, Type_Detector_r);
  Register #(.width(6)) Func (.D(R_Decode_func), .Q(Func_q), .clk(clock_1_out));  // open: en, clr
  Register #(.width(5)) ra (.D(R_Decode_ra), .Q(ra_q), .clk(clock_1_out));  // open: en, clr
  Register #(.width(5)) rb (.D(R_Decode_rb), .Q(rb_q), .clk(clock_1_out));  // open: en, clr
  Register #(.width(1)) MOVbit (.D(and_1_out), .Q(MOVbit_q), .clk(clock_1_out));  // open: en, clr
  ID_EX_Registers ID_EX (
    .Shamt(SHAMT_ALTER_shamt_2), .Op(R_Decode_opcode), .ra(registerfile_1_p7), .rb(registerfile_1_p8),
    .immediate(I_Decode_immediate), .rd(multiplexer_8_out), .ALUop(multiplexer_4_out),
    .PC(IF_ID_Pipeline_Register_pc_4_2), .in_9(clock_1_out), .Shamt_2(ID_EX_shamt_2), .Op_2(ID_EX_op_2),
    .ra_2(ID_EX_ra_2), .rb_2(ID_EX_rb_2), .immediate_2(ID_EX_immediate_2), .rd_2(ID_EX_rd_2),
    .ALUop_2(ID_EX_aluop_2), .PC_2(ID_EX_pc_2));
  Register #(.width(1)) R (.D(Type_Detector_r), .Q(R_q), .clk(clock_1_out));  // open: en, clr
  Register #(.width(1)) I (.D(Type_Detector_i), .Q(I_q), .clk(clock_1_out));  // open: en, clr
  Register #(.width(1)) WE (.D(Type_Detector_we), .Q(WE_q), .clk(clock_1_out));  // open: en, clr
  Register #(.width(1)) USECOMPARATOR (.D(multiplexer_5_out), .Q(USECOMPARATOR_q), .clk(clock_1_out));  // open: en, clr
  Register #(.width(1)) islink (.D(JUMP_decode_islink), .Q(islink_q), .clk(clock_1_out));  // open: en, clr
  ID_EX_mem_control_bits LOAD_STORE_CONTROL_BITS (
    .\unsigned (LOAD_STORE_DECODE_unsigned), .LOAD(multiplexer_7_out), .STORE(LOAD_STORE_DECODE_store),
    .WORD(LOAD_STORE_DECODE_word), .BYTE(LOAD_STORE_DECODE_byte), .CLOCK(clock_1_out),
    .UNSIGNED_2(LOAD_STORE_CONTROL_BITS_unsigned_2), .LOAD_2(LOAD_STORE_CONTROL_BITS_load_2),
    .STORE_2(LOAD_STORE_CONTROL_BITS_store_2), .WORD_2(LOAD_STORE_CONTROL_BITS_word_2),
    .BYTE_2(LOAD_STORE_CONTROL_BITS_byte_2));
  Register #(.width(1)) isreg (.D(JUMP_decode_isregjump), .Q(isreg_q), .clk(clock_1_out));  // open: en, clr
  Register #(.width(1)) isBranch (.D(Branch_Logic_isbranch), .clk(clock_1_out));  // open: en, Q, clr
  Multiplexer #(.width(32), .enable("false")) multiplexer_9 (
    .in0(ID_EX_ra_2), .in1(EX_MEM_result_2), .out(multiplexer_9_out), .sel(Forward_Unit_m_to_ex_forward_a));
  Multiplexer #(.width(32), .enable("false")) multiplexer_10 (
    .in0(ID_EX_rb_2), .in1(EX_MEM_result_2), .out(multiplexer_10_out), .sel(Forward_Unit_m_to_ex_forward_b));
  Multiplexer #(.width(32), .enable("false")) multiplexer_11 (
    .in0(multiplexer_9_out), .in1(registerfile_1_p1), .out(multiplexer_11_out),
    .sel(Forward_Unit_w_to_ex_forward_a));
  Multiplexer #(.width(32), .enable("false")) multiplexer_12 (
    .in0(multiplexer_10_out), .in1(registerfile_1_p1), .out(multiplexer_12_out),
    .sel(Forward_Unit_w_to_ex_forward_b));
  Forwarding_Unit Forward_Unit (
    .ID_Ex_ra(ra_q), .ID_Ex_rb(rb_q), .EX_Mem_rd(EX_MEM_rd_2), .Mem_WB_rd(registerfile_1_p4),
    .ID_EX_WE(WE_q), .Ex_Mem_WE(EX_MEM_we_2), .Mem_WB_WE(registerfile_1_p3),
    .M_to_EX_forward_A(Forward_Unit_m_to_ex_forward_a), .W_to_EX_forward_A(Forward_Unit_w_to_ex_forward_a),
    .M_to_EX_forward_B(Forward_Unit_m_to_ex_forward_b), .W_to_EX_forward_B(Forward_Unit_w_to_ex_forward_b));
  Multiplexer #(.width(32)) multiplexer_13 (
    .in0(multiplexer_12_out), .in1(ID_EX_immediate_2), .out(multiplexer_13_out), .sel(I_q));  // open: en
  Multiplexer #(.width(32)) multiplexer_14 (
    .in0(multiplexer_11_out), .in1({32{1'b0}}), .out(multiplexer_14_out), .sel(MOVbit_q));  // open: en
  Comparator Comparator (
    .A(multiplexer_11_out), .B(multiplexer_13_out), .Func(Func_q), .OP(ID_EX_op_2), .R(R_q),
    .Result(Comparator_result));
  // Mips_ALU mips_alu_1: pin names not known; wires that end beside it: multiplexer_14_out, multiplexer_13_out, ID_EX_aluop_2, ID_EX_shamt_2, mips_alu_1_p5
  Multiplexer #(.width(32)) multiplexer_15 (
    .in0(mips_alu_1_p5), .in1(Comparator_result), .out(multiplexer_15_out), .sel(USECOMPARATOR_q));  // open: en
  MOVSelector MOVSelector (
    .ALUResult(multiplexer_15_out), .A(multiplexer_11_out), .MOVbit(MOVbit_q), .MOV_WE(MOVSelector_mov_we),
    .Result(MOVSelector_result));
  and NO_MOV (NO_MOV_out, MOVSelector_mov_we, WE_q);
  Multiplexer #(.width(32)) multiplexer_16 (
    .in0(MOVSelector_result), .in1(ID_EX_pc_2), .out(multiplexer_16_out), .sel(or_2_out));  // open: en
  or or_2 (or_2_out, JAL_out, JALR_out);
  and JAL (JAL_out, islink_q, ~isreg_q);  // AND_Gate
  and JALR (JALR_out, islink_q, isreg_q);
  // Probe on ID_EX_rd_2
  MEM_WB EX_MEM (
    .MOVbit(MOVbit_q), .B_First(multiplexer_12_out), .Result(multiplexer_16_out), .ValB(multiplexer_13_out),
    .rd(ID_EX_rd_2), .OP(ID_EX_op_2), .R(R_q), .I(I_q), .WE(NO_MOV_out), .Clock(clock_1_out),
    .MOVbit_2(EX_MEM_movbit_2), .B_First_2(EX_MEM_b_first_2), .Result_2(EX_MEM_result_2),
    .ValB_2(EX_MEM_valb_2), .rd_2(EX_MEM_rd_2), .OP_2(EX_MEM_op_2), .R_2(EX_MEM_r_2), .I_2(EX_MEM_i_2),
    .WE_2(EX_MEM_we_2));
  Register #(.width(1)) islink_2 (.D(islink_q), .Q(islink_2_q), .clk(clock_1_out));  // open: en, clr
  Register #(.width(32)) PC_2 (.D(ID_EX_pc_2), .Q(PC_2_q), .clk(clock_1_out));  // open: en, clr
  ID_EX_mem_control_bits LOAD_STORE_CONTROL_BITS_2 (
    .\unsigned (LOAD_STORE_CONTROL_BITS_unsigned_2), .LOAD(LOAD_STORE_CONTROL_BITS_load_2),
    .STORE(LOAD_STORE_CONTROL_BITS_store_2), .WORD(LOAD_STORE_CONTROL_BITS_word_2),
    .BYTE(LOAD_STORE_CONTROL_BITS_byte_2), .CLOCK(clock_1_out),
    .UNSIGNED_2(LOAD_STORE_CONTROL_BITS_2_unsigned_2), .LOAD_2(LOAD_STORE_CONTROL_BITS_2_load_2),
    .STORE_2(LOAD_STORE_CONTROL_BITS_2_store_2), .WORD_2(LOAD_STORE_CONTROL_BITS_2_word_2),
    .BYTE_2(LOAD_STORE_CONTROL_BITS_2_byte_2));
  WORD_BYTE BYTE_decoder (.Target(EX_MEM_result_2), .Target_2(BYTE_decoder_target_2), .BYTE(BYTE_decoder_byte));
  Multiplexer #(.width(4)) multiplexer_17 (
    .in0(4'b0000), .in1(BYTE_decoder_byte), .out(multiplexer_17_out), .sel(LOAD_STORE_CONTROL_BITS_2_byte_2));  // open: en
  Multiplexer #(.width(4)) multiplexer_18 (
    .in0(multiplexer_17_out), .in1(4'b1111), .out(multiplexer_18_out), .sel(LOAD_STORE_CONTROL_BITS_2_word_2));  // open: en
  // MIPS_RAM mips_ram_1: pin names not known; wires that end beside it: BYTE_decoder_target_2, EX_MEM_b_first_2, LOAD_STORE_CONTROL_BITS_2_store_2, multiplexer_18_out, clock_1_out, LOAD_STORE_CONTROL_BITS_2_load_2, mips_ram_1_p7
  Multiplexer #(.width(32)) multiplexer_19 (
    .in0(EX_MEM_result_2), .in1(mips_ram_1_p7), .out(multiplexer_19_out),
    .sel(LOAD_STORE_CONTROL_BITS_2_load_2));  // open: en
  MEM_WB MEM_WB (
    .MOVbit(EX_MEM_movbit_2), .Result(multiplexer_19_out), .ValB(EX_MEM_valb_2), .rd(EX_MEM_rd_2),
    .OP(EX_MEM_op_2), .R(EX_MEM_r_2), .I(EX_MEM_i_2), .WE(EX_MEM_we_2), .Clock(clock_1_out),
    .Result_2(registerfile_1_p1), .rd_2(registerfile_1_p4), .WE_2(registerfile_1_p3));  // open: B_First, MOVbit_2, B_First_2, ValB_2, OP_2, R_2, I_2
  Register #(.width(1)) islink_3 (.D(islink_2_q), .clk(clock_1_out));  // open: en, Q, clr
  Register #(.width(32)) PC_3 (.D(PC_2_q), .clk(clock_1_out));  // open: en, Q, clr
  ID_EX_mem_control_bits LOAD_STORE_CONTROL_BITS_3 (
    .\unsigned (LOAD_STORE_CONTROL_BITS_2_unsigned_2), .LOAD(LOAD_STORE_CONTROL_BITS_2_load_2),
    .CLOCK(clock_1_out));  // open: STORE, WORD, BYTE, UNSIGNED_2, LOAD_2, STORE_2, WORD_2, BYTE_2
  // Probe on registerfile_1_p3
  // Probe on registerfile_1_p1

  // Notes on the sheet:
  //   branch/jump
  //   regjump
  //   stall
  //   FOR SLT
  //   ID/EX
  //   M to EX A
  //   B forwarding
  //   W to Ex A
  //   b4-b0
endmodule

module PC_4 (
  input  [31:0] PCin,
  output [31:0] PC_4
);

  Adder #(.width(30)) adder_1 (.a(PCin[31:2]), .b(30'h1), .out(PC_4[31:2]));  // open: cin, cout

  assign PC_4[1:0] = PCin[1:0];
endmodule

module IF_ID_Pipeline_Register (
  input  [31:0] Instruction,
  input  [31:0] PC_4,
  input  Clock,
  output [31:0] Instruction_2,
  output [31:0] PC_4_2
);

  Register #(.width(32)) u_PC_4 (.D(PC_4), .Q(PC_4_2), .clk(Clock));  // open: en, clr
  Register #(.width(32)) u_Instruction (.D(Instruction), .Q(Instruction_2), .clk(Clock));  // open: en, clr
endmodule

module Ins_Type_Decoder (
  input  [31:0] Instruction,
  output R,
  output I,
  output WE
);

  wire and_2_out, and_3_out, and_4_out, and_R_out, JAL_out, JALR_2_out, JALR_out, JR_out, LB_out, LBU_out,
       LW_out, not_1_out, not_2_out, not_3_out, not_4_out, not_5_out, not_6_out, not_7_out, not_8_out,
       not_9_out, not_10_out, not_11_out, not_12_out, or_2_out, or_3_out, or_4_out, WE_for_non_R_out;

  not not_1 (not_1_out, Instruction[31]);
  and WE_for_non_R (WE_for_non_R_out, not_1_out, Instruction[29]);
  not not_2 (not_2_out, Instruction[31]);
  not not_3 (not_3_out, Instruction[30]);
  not not_4 (not_4_out, Instruction[29]);
  not not_5 (not_5_out, Instruction[28]);
  not not_6 (not_6_out, Instruction[27]);
  not not_7 (not_7_out, Instruction[26]);
  not not_8 (not_8_out, Instruction[30]);
  not not_9 (not_9_out, Instruction[27]);
  and JALR (JALR_out, Instruction[0], ~Instruction[1], ~Instruction[2], Instruction[3], ~Instruction[4], ~Instruction[5]);  // AND_Gate
  and JR (JR_out, ~Instruction[0], ~Instruction[1], ~Instruction[2], Instruction[3], ~Instruction[4], ~Instruction[5]);  // AND_Gate
  and and_1 (R, not_2_out, not_3_out, not_4_out, not_5_out, not_6_out, not_7_out);
  and and_2 (and_2_out, not_8_out, not_9_out, Instruction[26]);
  or or_1 (I, and_2_out, Instruction[28], Instruction[29], Instruction[31]);
  or or_2 (or_2_out, JALR_out, JR_out);
  not not_10 (not_10_out, R);
  and and_3 (and_3_out, R, or_2_out);
  or or_3 (or_3_out, I, R);
  not not_11 (not_11_out, or_3_out);
  and and_4 (and_4_out, ~WE_for_non_R_out, not_10_out);  // AND_Gate
  not not_12 (not_12_out, or_4_out);
  or or_4 (or_4_out, not_11_out, and_4_out, and_3_out);
  and JALR_2 (JALR_2_out, Instruction[0], ~Instruction[1], ~Instruction[2], Instruction[3], ~Instruction[4], ~Instruction[5]);  // AND_Gate
  and JAL (JAL_out, Instruction[26], Instruction[27], ~Instruction[28], ~Instruction[29], ~Instruction[30], ~Instruction[31]);  // AND_Gate
  and LW (LW_out, Instruction[26], Instruction[27], ~Instruction[28], ~Instruction[29], ~Instruction[30], Instruction[31]);  // AND_Gate
  and LB (LB_out, ~Instruction[26], ~Instruction[27], ~Instruction[28], ~Instruction[29], ~Instruction[30], Instruction[31]);  // AND_Gate
  and LBU (LBU_out, ~Instruction[26], ~Instruction[27], Instruction[28], ~Instruction[29], ~Instruction[30], Instruction[31]);  // AND_Gate
  and and_R (and_R_out, R, JALR_2_out);
  or or_5 (WE, and_R_out, JAL_out, LW_out, LB_out, LBU_out, not_12_out);

  // Notes on the sheet:
  //   JAL, JALR, LW,LB,L
endmodule

module ID_EX_Registers (
  input  [4:0] Shamt,
  input  [5:0] Op,
  input  [31:0] ra,
  input  [31:0] rb,
  input  [31:0] immediate,
  input  [4:0] rd,
  input  [3:0] ALUop,
  input  [31:0] PC,
  input  in_9,
  output [4:0] Shamt_2,
  output [5:0] Op_2,
  output [31:0] ra_2,
  output [31:0] rb_2,
  output [31:0] immediate_2,
  output [4:0] rd_2,
  output [3:0] ALUop_2,
  output [31:0] PC_2
);

  Register #(.width(5)) u_Shamt (.D(Shamt), .Q(Shamt_2), .clk(in_9));  // open: en, clr
  Register #(.width(6)) u_Op (.D(Op), .Q(Op_2), .clk(in_9));  // open: en, clr
  Register #(.width(32)) u_ra (.D(ra), .Q(ra_2), .clk(in_9));  // open: en, clr
  Register #(.width(32)) u_rb (.D(rb), .Q(rb_2), .clk(in_9));  // open: en, clr
  Register #(.width(32)) u_immediate (.D(immediate), .Q(immediate_2), .clk(in_9));  // open: en, clr
  Register #(.width(5)) u_rd (.D(rd), .Q(rd_2), .clk(in_9));  // open: en, clr
  Register #(.width(4)) u_ALUop (.D(ALUop), .Q(ALUop_2), .clk(in_9));  // open: en, clr
  Register #(.width(32)) PC_4 (.D(PC), .Q(PC_2), .clk(in_9));  // open: en, clr
endmodule

module I_Type_Decoder (
  input  [31:0] Instruction,
  output [15:0] immediate,
  output [4:0] rd,
  output [4:0] rs,
  output [5:0] op
);


  assign immediate = Instruction[15:0];
  assign op = Instruction[31:26];
  assign rd = Instruction[25:21];
  assign rs = Instruction[20:16];
endmodule

module R_Decoder (
  input  [31:0] Instruction,
  output [5:0] func,
  output [4:0] shamt,
  output [4:0] rd,
  output [4:0] rb,
  output [4:0] ra,
  output [5:0] op
);


  assign func = Instruction[5:0];
  assign op = Instruction[31:26];
  assign ra = Instruction[25:21];
  assign rb = Instruction[20:16];
  assign rd = Instruction[15:11];
  assign shamt = Instruction[10:6];
endmodule

// I ALUop decode
module I_Type_ALUOP_Decoder (
  input  [5:0] Op,
  output [3:0] aluop
);

  wire and_1_out, and_2_out, not_1_out, not_2_out, not_3_out, not_4_out;
  wire [3:1] and_4_out;

  not not_1 (not_1_out, Op[1]);
  not not_2 (not_2_out, Op[0]);
  not not_3 (not_3_out, Op[1]);
  and and_1 (and_1_out, Op[5], ~Op[4]);  // AND_Gate
  not not_4 (not_4_out, Op[0]);
  and and_2 (and_2_out, Op[2], not_1_out);
  and and_3 (and_4_out[2], Op[1], not_2_out);
  and and_4 (and_4_out[1], not_3_out, Op[0]);
  or or_1 (and_4_out[3], not_4_out, and_2_out);
  Multiplexer #(.width(4)) multiplexer_1 (
    .in0({and_4_out, 1'b0}), .in1(4'b0010), .out(aluop), .sel(and_1_out));  // open: en
endmodule

module I_Everything (
  input  [31:0] in_1,
  output [31:0] immediate,
  output [4:0] rs,
  output [4:0] rd,
  output [3:0] ALUop,
  output useCOMPARATOR
);

  wire not_1_out, not_2_out, not_3_out;
  wire [5:0] Instruction_Splitter_op;
  wire [15:0] Instruction_Splitter_immediate;

  I_Type_Decoder Instruction_Splitter (
    .Instruction(in_1), .immediate(Instruction_Splitter_immediate), .rd(rs), .rs(rd),
    .op(Instruction_Splitter_op));
  I_Type_ALUOP_Decoder i_type_aluop_decoder_1 (.Op(Instruction_Splitter_op), .aluop(ALUop));
  I_Extender Bit_Extender (
    .immediate(Instruction_Splitter_immediate), .opcode(Instruction_Splitter_op), .immediate_2(immediate));
  not not_1 (not_1_out, Instruction_Splitter_op[5]);
  not not_2 (not_2_out, Instruction_Splitter_op[4]);
  not not_3 (not_3_out, Instruction_Splitter_op[2]);
  and and_1 (useCOMPARATOR, not_1_out, not_2_out, Instruction_Splitter_op[3], not_3_out, Instruction_Splitter_op[1]);
endmodule

module I_Extender (
  input  [15:0] immediate,
  input  [5:0] opcode,
  output [31:0] immediate_2
);

  wire and_1_out, and_2_out, and_3_out, and_4_out, and_5_out, not_1_out, not_2_out, not_3_out, not_4_out,
       not_5_out, not_6_out, not_7_out, not_8_out, not_9_out, or_1_out, or_2_out;
  wire [31:0] bit_extender_1_out, bit_extender_2_out, bit_extender_3_out, multiplexer_1_out;

  not not_1 (not_1_out, opcode[5]);
  not not_2 (not_2_out, opcode[4]);
  not not_3 (not_3_out, opcode[3]);
  not not_4 (not_4_out, opcode[1]);
  not not_5 (not_5_out, opcode[5]);
  not not_6 (not_6_out, opcode[4]);
  not not_7 (not_7_out, opcode[3]);
  and and_1 (and_1_out, not_1_out, not_2_out, not_3_out, not_4_out, opcode[0]);
  and and_2 (and_2_out, not_5_out, not_6_out, not_7_out, opcode[2]);
  or or_1 (or_1_out, and_1_out, and_2_out);
  assign bit_extender_1_out = {{16{immediate[15]}}, immediate};  // Bit_Extender bit_extender_1
  assign bit_extender_2_out = {{16{1'b0}}, immediate};  // Bit_Extender bit_extender_2
  assign bit_extender_3_out = {{14{immediate[15]}}, {immediate, 2'b00}};  // Bit_Extender bit_extender_3
  not not_8 (not_8_out, opcode[1]);
  not not_9 (not_9_out, opcode[0]);
  Multiplexer #(.width(32), .enable("false")) multiplexer_1 (
    .in0(bit_extender_1_out), .in1(bit_extender_3_out), .out(multiplexer_1_out), .sel(or_1_out));
  and and_3 (and_3_out, opcode[3], opcode[2], not_8_out);
  and and_4 (and_4_out, opcode[3], opcode[2], not_9_out);
  and and_5 (and_5_out, opcode[5], opcode[2]);
  or or_2 (or_2_out, and_3_out, and_4_out, and_5_out);
  Multiplexer #(.width(32)) multiplexer_2 (
    .in0(multiplexer_1_out), .in1(bit_extender_2_out), .out(immediate_2), .sel(or_2_out));  // open: en

  // Notes on the sheet:
  //   this logic sets SLL bit to 1 if it detects a branch instruction.
  //   determine whether I instruction requires zero extension
  //   if branch, first SLL 2 THEN extend
  //   pick between 16 or 18 bit sign extended imm
endmodule

module R_Everything (
  input  [31:0] Instruction,
  output [5:0] Func,
  output movbit,
  output [3:0] ALUop,
  output USECOMPARATOR,
  output [4:0] shamt,
  output [4:0] rd,
  output [4:0] rb,
  output [4:0] ra,
  output [5:0] opcode
);

  R_Decoder R_Ins_Splitter (
    .Instruction(Instruction), .func(Func), .shamt(shamt), .rd(rd), .rb(rb), .ra(ra), .op(opcode));
  R_mov_detector R_Mov_Detector (.func(Func), .MOVbit(movbit));
  R_Func_ALUop R_Func_ALUOP (.func(Func), .aluop(ALUop), .USECOMPARATOR(USECOMPARATOR));
endmodule

module R_Func_ALUop (
  input  [5:0] func,
  output [3:0] aluop,
  output USECOMPARATOR
);

  wire and_1_out, and_2_out, and_3_out, and_5_out, JALR_out, not_1_out, not_2_out, not_3_out, not_4_out;
  wire [3:0] or_3_out;

  and and_1 (and_1_out, func[5], func[2]);
  not not_1 (not_1_out, func[3]);
  and and_2 (and_2_out, func[3], func[0]);
  and and_3 (and_3_out, func[5], func[0]);
  not not_2 (not_2_out, func[5]);
  or or_1 (or_3_out[3], func[3], and_1_out);
  and and_4 (or_3_out[2], not_1_out, func[1]);
  or or_2 (or_3_out[1], and_2_out, and_3_out);
  and and_5 (and_5_out, not_2_out, func[0]);
  or or_3 (or_3_out[0], and_5_out, func[3]);
  not not_3 (not_3_out, func[4]);
  not not_4 (not_4_out, func[2]);
  and and_6 (USECOMPARATOR, func[5], not_3_out, func[3], not_4_out, func[1]);
  and JALR (JALR_out, ~func[5], ~func[4], func[3], ~func[2], ~func[1], func[0]);  // AND_Gate
  Multiplexer #(.width(4)) multiplexer_1 (.in0(or_3_out), .in1(4'b0010), .out(aluop), .sel(JALR_out));  // open: en
endmodule

module I_compataor (
  input  [5:0] opcode,
  output dontuseALU
);

  wire not_1_out, not_2_out, not_3_out;

  not not_1 (not_1_out, opcode[5]);
  not not_2 (not_2_out, opcode[4]);
  not not_3 (not_3_out, opcode[2]);
  and and_1 (dontuseALU, not_1_out, not_2_out, opcode[3], not_3_out, opcode[1]);
endmodule

module MEM_WB (
  input  MOVbit,
  input  [31:0] B_First,
  input  [31:0] Result,
  input  [31:0] ValB,
  input  [4:0] rd,
  input  [5:0] OP,
  input  R,
  input  I,
  input  WE,
  input  Clock,
  output MOVbit_2,
  output [31:0] B_First_2,
  output [31:0] Result_2,
  output [31:0] ValB_2,
  output [4:0] rd_2,
  output [5:0] OP_2,
  output R_2,
  output I_2,
  output WE_2
);

  Register #(.width(1)) register_1 (.D(MOVbit), .Q(MOVbit_2), .clk(Clock));  // open: en, clr
  Register #(.width(32)) register_2 (.D(B_First), .Q(B_First_2), .clk(Clock));  // open: en, clr
  Register #(.width(32)) register_3 (.D(Result), .Q(Result_2), .clk(Clock));  // open: en, clr
  Register #(.width(32)) register_4 (.D(ValB), .Q(ValB_2), .clk(Clock));  // open: en, clr
  Register #(.width(5)) register_5 (.D(rd), .Q(rd_2), .clk(Clock));  // open: en, clr
  Register #(.width(6)) register_6 (.D(OP), .Q(OP_2), .clk(Clock));  // open: en, clr
  Register #(.width(1)) register_7 (.D(R), .Q(R_2), .clk(Clock));  // open: en, clr
  Register #(.width(1)) register_8 (.D(I), .Q(I_2), .clk(Clock));  // open: en, clr
  Register #(.width(1)) register_9 (.D(WE), .Q(WE_2), .clk(Clock));  // open: en, clr
endmodule

module R_mov_detector (
  input  [5:0] func,
  output MOVbit
);

  wire MOVN_out, MOVZ_out;

  and MOVZ (MOVZ_out, ~func[0], func[1], ~func[2], func[3], ~func[4], ~func[5]);  // AND_Gate
  and MOVN (MOVN_out, func[0], func[1], ~func[2], func[3], ~func[4], ~func[5]);  // AND_Gate
  or or_1 (MOVbit, MOVZ_out, MOVN_out);
endmodule

module MOVSelector (
  input  MOVbit,
  input  [31:0] ALUResult,
  input  [31:0] A,
  output [31:0] Result,
  output MOV_WE
);

  wire and_1_out;

  Multiplexer #(.width(32), .enable("false")) multiplexer_1 (.in0(ALUResult), .in1(A), .out(Result), .sel(MOVbit));
  and and_1 (and_1_out, MOVbit, ALUResult[0]);
  Multiplexer #(.enable("false")) multiplexer_2 (.in0(1'b1), .in1(and_1_out), .out(MOV_WE), .sel(MOVbit));
endmodule

module Comparator (
  input  [31:0] A,
  input  [31:0] B,
  input  [5:0] Func,
  input  [5:0] OP,
  input  R,
  output [31:0] Result
);

  wire comparator_1_lt, comparator_2_lt, I_Detector_signed, multiplexer_1_out, multiplexer_2_out,
       R_Detector_signed;

  CompSignR R_Detector (.Func(Func), .Signed(R_Detector_signed));
  CompSignI I_Detector (.OP(OP), .Signed(I_Detector_signed));
  Multiplexer multiplexer_1 (
    .in0(I_Detector_signed), .in1(R_Detector_signed), .out(multiplexer_1_out), .sel(R));  // open: en
  Comparator_part #(.width(32), .mode("unsigned")) comparator_1 (.a(A), .b(B), .lt(comparator_1_lt));  // open: gt, eq
  Comparator_part #(.width(32)) comparator_2 (.a(A), .b(B), .lt(comparator_2_lt));  // open: gt, eq
  Multiplexer multiplexer_2 (
    .in0(comparator_1_lt), .in1(comparator_2_lt), .out(multiplexer_2_out), .sel(multiplexer_1_out));  // open: en
  assign Result = {{31{1'b0}}, multiplexer_2_out};  // Bit_Extender bit_extender_1

  // Notes on the sheet:
  //   Decides Signed or Unsigned
endmodule

module CompSignR (
  input  [5:0] Func,
  output Signed
);

  not not_1 (Signed, Func[0]);

  // Notes on the sheet:
  //   First Bit Decides
endmodule

module CompSignI (
  input  [5:0] OP,
  output Signed
);

  not not_1 (Signed, OP[0]);

  // Notes on the sheet:
  //   First Bit Decides
endmodule

module Forwarding_Unit (
  input  [4:0] ID_Ex_ra,
  input  [4:0] ID_Ex_rb,
  input  [4:0] EX_Mem_rd,
  input  [4:0] Mem_WB_rd,
  input  ID_EX_WE,
  input  Ex_Mem_WE,
  input  Mem_WB_WE,
  output M_to_EX_forward_A,
  output W_to_EX_forward_A,
  output M_to_EX_forward_B,
  output W_to_EX_forward_B
);

  wire _0_2_out, _0_out, and_1_out, and_2_out, not_1_out, not_2_out, ra__rd_out, ra__xmem_rd_out, rb__rd_out,
       rb_xm_rd_out;
  wire [4:0] xnor_1_out, xnor_2_out, xnor_3_out, xnor_4_out;

  assign xnor_1_out = ~(ID_Ex_ra ^ Mem_WB_rd);  // XNOR_Gate xnor_1, 5 bits wide
  assign xnor_2_out = ~(ID_Ex_rb ^ Mem_WB_rd);  // XNOR_Gate xnor_2, 5 bits wide
  or _0 (_0_out, Mem_WB_rd[0], Mem_WB_rd[1], Mem_WB_rd[2], Mem_WB_rd[3], Mem_WB_rd[4]);
  assign xnor_3_out = ~(ID_Ex_ra ^ EX_Mem_rd);  // XNOR_Gate xnor_3, 5 bits wide
  assign xnor_4_out = ~(ID_Ex_rb ^ EX_Mem_rd);  // XNOR_Gate xnor_4, 5 bits wide
  or _0_2 (_0_2_out, EX_Mem_rd[0], EX_Mem_rd[1], EX_Mem_rd[2], EX_Mem_rd[3], EX_Mem_rd[4]);
  and ra__rd (ra__rd_out, xnor_1_out[0], xnor_1_out[1], xnor_1_out[2], xnor_1_out[3], xnor_1_out[4]);
  and rb__rd (rb__rd_out, xnor_2_out[0], xnor_2_out[1], xnor_2_out[2], xnor_2_out[3], xnor_2_out[4]);
  and ra__xmem_rd (ra__xmem_rd_out, xnor_3_out[0], xnor_3_out[1], xnor_3_out[2], xnor_3_out[3], xnor_3_out[4]);
  and rb_xm_rd (rb_xm_rd_out, xnor_4_out[0], xnor_4_out[1], xnor_4_out[2], xnor_4_out[3], xnor_4_out[4]);
  and and_1 (and_1_out, ra__xmem_rd_out, _0_2_out, ID_EX_WE);
  and and_2 (and_2_out, rb_xm_rd_out, _0_out, ID_EX_WE);
  not not_1 (not_1_out, and_1_out);
  and and_3 (M_to_EX_forward_A, ra__xmem_rd_out, _0_2_out, Ex_Mem_WE);
  and and_4 (M_to_EX_forward_B, rb_xm_rd_out, _0_2_out, Ex_Mem_WE);
  and and_5 (W_to_EX_forward_A, ra__rd_out, _0_out, Mem_WB_WE, not_1_out);
  not not_2 (not_2_out, and_2_out);
  and and_6 (W_to_EX_forward_B, rb__rd_out, _0_out, Ex_Mem_WE, not_2_out);
endmodule

module SHAMT_Decoder (
  input  [5:0] OpCode,
  input  [4:0] Shamt,
  input  [5:0] Func,
  input  [31:0] A,
  output [4:0] SHAMT_2
);

  wire IsLUI_islui, IsVAR_isvar;
  wire [4:0] multiplexer_1_out;

  LUI_Decoder IsLUI (.OP(OpCode), .IsLUI(IsLUI_islui));
  SLLV_SLL_Decoder IsVAR (.OP(OpCode), .Func(Func), .IsVar(IsVAR_isvar));
  Multiplexer #(.width(5)) multiplexer_1 (
    .in0(Shamt), .in1(A[4:0]), .out(multiplexer_1_out), .sel(IsVAR_isvar));  // open: en
  Multiplexer #(.width(5)) multiplexer_2 (
    .in0(multiplexer_1_out), .in1(5'b10000), .out(SHAMT_2), .sel(IsLUI_islui));  // open: en
endmodule

module LUI_Decoder (
  input  [5:0] OP,
  output IsLUI
);

  wire not_1_out, not_2_out;

  not not_1 (not_1_out, OP[5]);
  not not_2 (not_2_out, OP[4]);
  and and_1 (IsLUI, not_1_out, not_2_out, OP[3], OP[2], OP[1], OP[0]);
endmodule

module SLLV_SLL_Decoder (
  input  [5:0] OP,
  input  [5:0] Func,
  output IsVar
);

  wire and_1_out, and_2_out, and_3_out, not_1_out, not_2_out, not_3_out, not_4_out, not_5_out, not_6_out,
       not_7_out, or_1_out;

  and and_1 (and_1_out, ~OP[5], ~OP[4], ~OP[3], ~OP[2], ~OP[1], ~OP[0]);  // AND_Gate
  not not_1 (not_1_out, Func[5]);
  not not_2 (not_2_out, Func[4]);
  not not_3 (not_3_out, Func[3]);
  not not_4 (not_4_out, Func[0]);
  not not_5 (not_5_out, Func[5]);
  not not_6 (not_6_out, Func[4]);
  not not_7 (not_7_out, Func[3]);
  and and_2 (and_2_out, not_1_out, not_2_out, not_3_out, Func[2], not_4_out);
  and and_3 (and_3_out, not_5_out, not_6_out, not_7_out, Func[2], Func[1]);
  or or_1 (or_1_out, and_2_out, and_3_out);
  and and_4 (IsVar, and_1_out, or_1_out);
endmodule

module BrachControlSignal (
  input  EQ,
  input  NE,
  input  GEZ,
  input  LTZ,
  input  LEZ,
  input  GTZ,
  output b2,
  output b1,
  output b0
);

  wire not_1_out, not_2_out, not_3_out, not_4_out, not_5_out, not_6_out, not_7_out, not_8_out, not_9_out,
       not_10_out, not_11_out;

  not not_1 (not_1_out, GEZ);
  not not_2 (not_2_out, LTZ);
  not not_3 (not_3_out, LEZ);
  not not_4 (not_4_out, GTZ);
  not not_5 (not_5_out, EQ);
  not not_6 (not_6_out, NE);
  not not_7 (not_7_out, LEZ);
  not not_8 (not_8_out, GTZ);
  not not_9 (not_9_out, NE);
  not not_10 (not_10_out, LTZ);
  not not_11 (not_11_out, GTZ);
  and and_1 (b2, not_1_out, not_2_out, not_3_out, not_4_out);
  and and_2 (b1, not_5_out, not_6_out, not_7_out, not_8_out);
  and and_3 (b0, not_9_out, not_10_out, not_11_out);
endmodule

module BLTZ_BGEZ (
  input  [5:0] OP,
  input  [4:0] b20_16,
  output GEZ,
  output LTZ
);

  wire BGEZ_out, BLTZ_out, not_1_out;

  and BGEZ (BGEZ_out, OP[0], ~OP[1], ~OP[2], ~OP[3], ~OP[4], ~OP[5]);  // AND_Gate
  and BLTZ (BLTZ_out, OP[0], ~OP[1], ~OP[2], ~OP[3], ~OP[4], ~OP[5]);  // AND_Gate
  not not_1 (not_1_out, b20_16[0]);
  and and_1 (GEZ, BGEZ_out, b20_16[0]);
  and and_2 (LTZ, BLTZ_out, not_1_out);
endmodule

module BranchType (
  input  [5:0] OP,
  input  [4:0] b20_16,
  output [2:0] out_3
);

  wire BEQ_out, BGTZ_out, BLEZ_out, BLTZ_BGEZ_gez, BLTZ_BGEZ_ltz, BNE_out, not_1_out, not_2_out, not_3_out,
       not_4_out, not_5_out, not_6_out, not_7_out, not_8_out, not_9_out, not_10_out, not_11_out;

  BLTZ_BGEZ BLTZ_BGEZ (.OP(OP), .b20_16(b20_16), .GEZ(BLTZ_BGEZ_gez), .LTZ(BLTZ_BGEZ_ltz));
  and BLEZ (BLEZ_out, ~OP[0], OP[1], OP[2], ~OP[3], ~OP[4], ~OP[5]);  // AND_Gate
  and BGTZ (BGTZ_out, OP[0], OP[1], OP[2], ~OP[3], ~OP[4], ~OP[5]);  // AND_Gate
  and BEQ (BEQ_out, ~OP[0], ~OP[1], OP[2], ~OP[3], ~OP[4], ~OP[5]);  // AND_Gate
  and BNE (BNE_out, OP[0], ~OP[1], OP[2], ~OP[3], ~OP[4], ~OP[5]);  // AND_Gate
  // Probe on BEQ_out
  // Probe on BNE_out
  // Probe on BLTZ_BGEZ_gez
  // Probe on BLTZ_BGEZ_ltz
  // Probe on BLEZ_out
  // Probe on BGTZ_out
  not not_1 (not_1_out, BLTZ_BGEZ_gez);
  not not_2 (not_2_out, BLTZ_BGEZ_ltz);
  not not_3 (not_3_out, BLEZ_out);
  not not_4 (not_4_out, BGTZ_out);
  not not_5 (not_5_out, BEQ_out);
  not not_6 (not_6_out, BNE_out);
  not not_7 (not_7_out, BLEZ_out);
  not not_8 (not_8_out, BGTZ_out);
  not not_9 (not_9_out, BNE_out);
  not not_10 (not_10_out, BLTZ_BGEZ_ltz);
  not not_11 (not_11_out, BGTZ_out);
  and and_1 (out_3[2], not_1_out, not_2_out, not_3_out, not_4_out);
  and and_2 (out_3[1], not_5_out, not_6_out, not_7_out, not_8_out);
  and and_3 (out_3[0], not_9_out, not_10_out, not_11_out);

  // Notes on the sheet:
  //   Control bit for mux
endmodule

module BranchIsVar (
  input  [5:0] OP,
  output BranchIsVar
);

  wire BEQ_out, BNE_out;

  and BEQ (BEQ_out, ~OP[0], ~OP[1], OP[2], ~OP[3], ~OP[4], ~OP[5]);  // AND_Gate
  and BNE (BNE_out, OP[0], ~OP[1], OP[2], ~OP[3], ~OP[4], ~OP[5]);  // AND_Gate
  or or_1 (BranchIsVar, BEQ_out, BNE_out);
endmodule

module BRANCH_HARDWARE (
  input  [31:0] A,
  input  [31:0] B,
  input  [31:0] INSTR,
  output BranchBool
);

  wire comparator_1_eq, comparator_1_gt, comparator_1_lt, IsVar_branchisvar, not_1_out, or_1_out, or_2_out;
  wire [2:0] branchtype_1_out_3;
  wire [31:0] multiplexer_1_out;

  BranchIsVar IsVar (.OP(INSTR[31:26]), .BranchIsVar(IsVar_branchisvar));
  BranchType branchtype_1 (.OP(INSTR[31:26]), .b20_16(INSTR[20:16]), .out_3(branchtype_1_out_3));
  Multiplexer #(.width(32)) multiplexer_1 (
    .in0({32{1'b0}}), .in1(B), .out(multiplexer_1_out), .sel(IsVar_branchisvar));  // open: en
  Comparator_part #(.width(32)) comparator_1 (
    .a(A), .b(multiplexer_1_out), .gt(comparator_1_gt), .eq(comparator_1_eq), .lt(comparator_1_lt));
  or or_1 (or_1_out, comparator_1_eq, comparator_1_lt);
  or or_2 (or_2_out, comparator_1_gt, comparator_1_eq);
  not not_1 (not_1_out, comparator_1_eq);
  // Probe on branchtype_1_out_3
  Multiplexer #(.select(3)) multiplexer_2 (
    .in0(comparator_1_gt), .in1(comparator_1_lt), .in2(or_1_out), .in3(or_2_out), .in4(not_1_out),
    .in5(comparator_1_eq), .in6(1'b0), .in7(1'b0), .out(BranchBool), .sel(branchtype_1_out_3));  // open: en

  // Notes on the sheet:
  //   returns 7 if its not a branch
endmodule

module PC_BRANCH_HARDWARE (
  input  [31:0] PC,
  input  [31:0] Immediate,
  input  [31:0] A,
  input  IsJump,
  input  [31:0] B,
  input  [31:0] INSTR,
  output [31:0] out_7,
  output Branch_Jump_Bool,
  output IsBranch
);

  wire [31:0] adder_1_out, adder_2_out, bit_extender_1_out, multiplexer_1_out, shifter_1_out;

  assign bit_extender_1_out = {{6{INSTR[25]}}, INSTR[25:0]};  // Bit_Extender bit_extender_1
  // Probe on Immediate
  Shifter #(.width(32)) shifter_1 (.in(bit_extender_1_out), .\dist (5'b00010), .out(shifter_1_out));
  Adder #(.width(32)) adder_1 (.a(32'h4), .b(PC), .out(adder_1_out));  // open: cin, cout
  Adder #(.width(32)) adder_2 (.a(PC), .b(Immediate), .out(adder_2_out));  // open: cin, cout
  Multiplexer #(.width(32)) multiplexer_1 (
    .in0(adder_2_out), .in1(shifter_1_out), .out(multiplexer_1_out), .sel(IsJump));  // open: en
  or or_1 (Branch_Jump_Bool, IsBranch, IsJump);
  BRANCH_HARDWARE branch_hardware_1 (.A(A), .B(B), .INSTR(INSTR), .BranchBool(IsBranch));
  Multiplexer #(.width(32)) multiplexer_2 (
    .in0(adder_1_out), .in1(multiplexer_1_out), .out(out_7), .sel(Branch_Jump_Bool));  // open: en

  // Notes on the sheet:
  //   PC VALUE
endmodule

module stall_unit (
  input  ID_EX_MEMREAD,
  input  [4:0] IF_ID_RA,
  input  [4:0] ID_EX_rd,
  input  [4:0] IF_ID_RB,
  output STALL
);

  wire and_1_out, and_2_out, or_1_out;
  wire [4:0] xnor_1_out, xnor_2_out;

  assign xnor_1_out = ~(IF_ID_RA ^ ID_EX_rd);  // XNOR_Gate xnor_1, 5 bits wide
  assign xnor_2_out = ~(ID_EX_rd ^ IF_ID_RB);  // XNOR_Gate xnor_2, 5 bits wide
  and and_1 (and_1_out, xnor_1_out[0], xnor_1_out[1], xnor_1_out[2], xnor_1_out[3], xnor_1_out[4]);
  and and_2 (and_2_out, xnor_2_out[0], xnor_2_out[1], xnor_2_out[2], xnor_2_out[3], xnor_2_out[4]);
  or or_1 (or_1_out, and_1_out, and_2_out);
  and and_3 (STALL, ID_EX_MEMREAD, or_1_out);
endmodule

module ID_EX_mem_control_bits (
  input  \unsigned ,
  input  LOAD,
  input  STORE,
  input  WORD,
  input  BYTE,
  input  CLOCK,
  output UNSIGNED_2,
  output LOAD_2,
  output STORE_2,
  output WORD_2,
  output BYTE_2
);

  Register #(.width(1)) register_1 (.D(\unsigned ), .Q(UNSIGNED_2), .clk(CLOCK));  // open: en, clr
  Register #(.width(1)) register_2 (.D(LOAD), .Q(LOAD_2), .clk(CLOCK));  // open: en, clr
  Register #(.width(1)) register_3 (.D(STORE), .Q(STORE_2), .clk(CLOCK));  // open: en, clr
  Register #(.width(1)) register_4 (.D(WORD), .Q(WORD_2), .clk(CLOCK));  // open: en, clr
  Register #(.width(1)) register_5 (.D(BYTE), .Q(BYTE_2), .clk(CLOCK));  // open: en, clr
endmodule

module LOAD_STORE_HARDWARE (
  input  [5:0] in_1,
  output Unsigned,
  output Load,
  output Store,
  output WORD,
  output BYTE
);

  wire LB_out, LBU_out, LW_out, not_1_out, or_3_out, SB_out, SW_out;

  and LB (LB_out, ~in_1[0], ~in_1[1], ~in_1[2], ~in_1[3], ~in_1[4], in_1[5]);  // AND_Gate
  and LW (LW_out, in_1[0], in_1[1], ~in_1[2], ~in_1[3], ~in_1[4], in_1[5]);  // AND_Gate
  and LBU (LBU_out, ~in_1[0], ~in_1[1], in_1[2], ~in_1[3], ~in_1[4], in_1[5]);  // AND_Gate
  and SB (SB_out, ~in_1[0], ~in_1[1], ~in_1[2], in_1[3], ~in_1[4], in_1[5]);  // AND_Gate
  and SW (SW_out, in_1[0], in_1[1], ~in_1[2], in_1[3], ~in_1[4], in_1[5]);  // AND_Gate
  or or_1 (BYTE, LB_out, LBU_out, SB_out);
  or or_2 (WORD, LW_out, SW_out);
  or or_3 (or_3_out, LB_out, LW_out);
  or or_4 (Load, LB_out, LW_out, LBU_out);
  or or_5 (Store, SB_out, SW_out);
  not not_1 (not_1_out, or_3_out);
  and and_1 (Unsigned, not_1_out, LBU_out);
endmodule

module WORD_BYTE (
  input  [31:0] Target,
  output [19:0] Target_2,
  output [3:0] BYTE
);

  wire [1:0] xor_1_out;
  wire [31:20] shifter_1_out;

  Shifter #(.width(32), .shift("lr")) shifter_1 (.in(Target), .\dist (5'b00010), .out({shifter_1_out, Target_2}));
  assign xor_1_out = Target[1:0] ^ 2'b00;  // XOR_Gate xor_1, 2 bits wide
  // Probe on xor_1_out
  Multiplexer #(.select(2), .width(4)) multiplexer_1 (
    .in0(4'b0001), .in1(4'b0010), .in2(4'b0100), .in3(4'b1000), .out(BYTE), .sel(xor_1_out));  // open: en
endmodule

module JUMP_DECODE (
  input  [31:0] INSTR,
  output IsRegJump,
  output IsLink,
  output IsJump
);

  wire and_1_out, and_2_out, J_out, JAL_out, JALR_out, JR_out, R_Type_out;

  and JALR (JALR_out, INSTR[0], ~INSTR[1], ~INSTR[2], INSTR[3], ~INSTR[4], ~INSTR[5]);  // AND_Gate
  and R_Type (R_Type_out, ~INSTR[26], ~INSTR[27], ~INSTR[28], ~INSTR[29], ~INSTR[30], ~INSTR[31]);  // AND_Gate
  and JR (JR_out, ~INSTR[0], ~INSTR[1], ~INSTR[2], INSTR[3], ~INSTR[4], ~INSTR[5]);  // AND_Gate
  and and_1 (and_1_out, R_Type_out, JR_out);
  and and_2 (and_2_out, R_Type_out, JALR_out);
  and JAL (JAL_out, INSTR[26], INSTR[27], ~INSTR[28], ~INSTR[29], ~INSTR[30], ~INSTR[31]);  // AND_Gate
  and J (J_out, ~INSTR[26], INSTR[27], ~INSTR[28], ~INSTR[29], ~INSTR[30], ~INSTR[31]);  // AND_Gate
  or or_1 (IsRegJump, and_1_out, and_2_out);
  or or_2 (IsLink, and_2_out, JAL_out);
  or or_3 (IsJump, JAL_out, and_2_out, and_1_out, J_out);
endmodule

module NonBoolBranch (
  input  [31:0] INSTR,
  output IsBranchType
);

  wire BEQ_out, BGTZ_out, BLEZ_out, BLTZ_BGEZ_gez, BLTZ_BGEZ_ltz, BNE_out;

  BLTZ_BGEZ BLTZ_BGEZ (.OP(INSTR[31:26]), .b20_16(INSTR[20:16]), .GEZ(BLTZ_BGEZ_gez), .LTZ(BLTZ_BGEZ_ltz));
  and BLEZ (BLEZ_out, ~INSTR[26], INSTR[27], INSTR[28], ~INSTR[29], ~INSTR[30], ~INSTR[31]);  // AND_Gate
  and BGTZ (BGTZ_out, INSTR[26], INSTR[27], INSTR[28], ~INSTR[29], ~INSTR[30], ~INSTR[31]);  // AND_Gate
  and BEQ (BEQ_out, ~INSTR[26], ~INSTR[27], INSTR[28], ~INSTR[29], ~INSTR[30], ~INSTR[31]);  // AND_Gate
  and BNE (BNE_out, INSTR[26], ~INSTR[27], INSTR[28], ~INSTR[29], ~INSTR[30], ~INSTR[31]);  // AND_Gate
  // Probe on BEQ_out
  // Probe on BNE_out
  // Probe on BLTZ_BGEZ_gez
  // Probe on BLTZ_BGEZ_ltz
  // Probe on BLEZ_out
  // Probe on BGTZ_out
  or or_1 (IsBranchType, BEQ_out, BNE_out, BLTZ_BGEZ_gez, BLTZ_BGEZ_ltz, BLEZ_out, BGTZ_out);
endmodule
