// Logisim project MIPS32.REVISED.circ as structural Verilog: 22 circuits, main circuit main
module main (
);

  wire clock_1_out, EX_MEM_i_2, EX_MEM_movbit_2, EX_MEM_r_2, EX_MEM_we_2, I_Decode_usecomparator, I_q,
       MOVbit_q, MOVSelector_mov_we, multiplexer_5_out, NO_MOV_out, not_1_out, R_Decode_movbit,
       R_Decode_usecomparator, R_q, registerfile_1_p3, registerfile_1_p5, Type_Detector_p2, Type_Detector_p3,
       Type_Detector_p4, USECOMPARATOR_q, WE_q;
  wire [3:0] I_Decode_aluop, ID_EX_aluop_2, multiplexer_1_out, R_Decode_aluop;
  wire [4:0] EX_MEM_rd_2, I_Decode_rd, ID_EX_rd_2, ID_EX_shamt_2, multiplexer_2_out, multiplexer_4_out,
       multiplexer_7_out, R_Decode_ra, R_Decode_rb, R_Decode_rd, R_Decode_shamt, registerfile_1_p4,
       registerfile_1_p7;
  wire [5:0] EX_MEM_op_2, ID_EX_op_2, R_Decode_opcode;
  wire [31:0] Comparator_result, EX_MEM_result_2, EX_MEM_valb_2, I_Decode_immediate, ID_EX_immediate_2,
       ID_EX_pc_2, ID_EX_ra_2, ID_EX_rb_2, IF_ID_Pipeline_Register_instruction_2,
       IF_ID_Pipeline_Register_pc_4_2, mips_alu_1_p5, mipsprogramrom_1_p2, MOVSelector_result,
       multiplexer_6_out, multiplexer_8_out, PC_2_q, PC___4_pc_4, PC_q, registerfile_1_p1, registerfile_1_p8,
       registerfile_1_p9;

  PC_4 PC___4 (.PCin(PC_q), .PC_4(PC___4_pc_4));
  Clock clock_1 (.out(clock_1_out));
  Register #(.width(32)) PC (.D(PC___4_pc_4), .Q(PC_q), .clk(clock_1_out));  // open: en, clr
  // MIPSProgramROM mipsprogramrom_1: pin names not known; wires that end beside it: PC_q, mipsprogramrom_1_p2
  IF_ID_Pipeline_Register IF_ID_Pipeline_Register (
    .Instruction(mipsprogramrom_1_p2), .PC_4(PC___4_pc_4), .Clock(clock_1_out),
    .Instruction_2(IF_ID_Pipeline_Register_instruction_2), .PC_4_2(IF_ID_Pipeline_Register_pc_4_2));
  R_Everything R_Decode (
    .Instruction(IF_ID_Pipeline_Register_instruction_2), .movbit(R_Decode_movbit), .ALUop(R_Decode_aluop),
    .USECOMPARATOR(R_Decode_usecomparator), .shamt(R_Decode_shamt), .rd(R_Decode_rd), .rb(R_Decode_rb),
    .ra(R_Decode_ra), .opcode(R_Decode_opcode));  // open: Func
  // Ins_Type_Decoder Type_Detector: pin names not known; wires that end beside it: IF_ID_Pipeline_Register_instruction_2, Type_Detector_p2, Type_Detector_p3, Type_Detector_p4
  I_Everything I_Decode (
    .in_1(IF_ID_Pipeline_Register_instruction_2), .immediate(I_Decode_immediate), .rd(I_Decode_rd),
    .ALUop(I_Decode_aluop), .useCOMPARATOR(I_Decode_usecomparator));  // open: rs
  Multiplexer #(.width(4)) multiplexer_1 (
    .in0(R_Decode_aluop), .in1(I_Decode_aluop), .out(multiplexer_1_out), .sel(Type_Detector_p2));  // open: en
  Multiplexer #(.width(5), .enable("false")) multiplexer_2 (
    .in0(R_Decode_ra), .in1({5{1'b0}}), .out(multiplexer_2_out), .sel(registerfile_1_p5));
  // RegisterFile registerfile_1: pin names not known; wires that end beside it: registerfile_1_p1, clock_1_out, registerfile_1_p3, registerfile_1_p4, registerfile_1_p5, multiplexer_2_out, registerfile_1_p7, registerfile_1_p8, registerfile_1_p9
  Multiplexer #(.width(5)) multiplexer_3 (
    .in1(R_Decode_rb), .out(registerfile_1_p7), .sel(Type_Detector_p2));  // open: in0, en
  Multiplexer #(.width(5)) multiplexer_4 (
    .in0(I_Decode_rd), .in1(R_Decode_rd), .out(multiplexer_4_out), .sel(Type_Detector_p2));  // open: en
  Multiplexer #(.enable("false")) multiplexer_5 (
    .in0(I_Decode_usecomparator), .in1(R_Decode_usecomparator), .out(multiplexer_5_out),
    .sel(Type_Detector_p2));
  and and_1 (registerfile_1_p5, R_Decode_movbit, Type_Detector_p2);
  not not_1 (not_1_out, Type_Detector_p4);
  Register #(.width(1)) MOVbit (.D(registerfile_1_p5), .Q(MOVbit_q), .clk(clock_1_out));  // open: en, clr
  ID_EX_Registers ID_EX (
    .Shamt(R_Decode_shamt), .Op(R_Decode_opcode), .ra(registerfile_1_p8), .rb(registerfile_1_p9),
    .immediate(I_Decode_immediate), .rd(multiplexer_4_out), .ALUop(multiplexer_1_out),
    .PC(IF_ID_Pipeline_Register_pc_4_2), .in_9(clock_1_out), .Shamt_2(ID_EX_shamt_2), .Op_2(ID_EX_op_2),
    .ra_2(ID_EX_ra_2), .rb_2(ID_EX_rb_2), .immediate_2(ID_EX_immediate_2), .rd_2(ID_EX_rd_2),
    .ALUop_2(ID_EX_aluop_2), .PC_2(ID_EX_pc_2));
  Register #(.width(1)) R (.D(Type_Detector_p2), .Q(R_q), .clk(clock_1_out));  // open: en, clr
  Register #(.width(1)) I (.D(Type_Detector_p3), .Q(I_q), .clk(clock_1_out));  // open: en, clr
  Register #(.width(1)) WE (.D(not_1_out), .Q(WE_q), .clk(clock_1_out));  // open: en, clr
  Register #(.width(1)) USECOMPARATOR (.D(multiplexer_5_out), .Q(USECOMPARATOR_q), .clk(clock_1_out));  // open: en, clr
  Multiplexer #(.width(32)) multiplexer_6 (
    .in0(ID_EX_rb_2), .in1(ID_EX_immediate_2), .out(multiplexer_6_out), .sel(I_q));  // open: en
  Multiplexer #(.width(5)) multiplexer_7 (
    .in0(ID_EX_shamt_2), .in1(ID_EX_immediate_2[4:0]), .out(multiplexer_7_out), .sel(ID_EX_op_2[2]));  // open: en
  Comparator Comparator (
    .A(ID_EX_ra_2), .B(multiplexer_6_out), .aluOP(ID_EX_aluop_2), .OP(ID_EX_op_2), .R(R_q),
    .Result(Comparator_result));
  // Mips_ALU mips_alu_1: pin names not known; wires that end beside it: ID_EX_ra_2, multiplexer_6_out, ID_EX_aluop_2, multiplexer_7_out, mips_alu_1_p5
  Multiplexer #(.width(32)) multiplexer_8 (
    .in0(Comparator_result), .in1(mips_alu_1_p5), .out(multiplexer_8_out), .sel(USECOMPARATOR_q));  // open: en
  MOVSelector MOVSelector (
    .ALUResult(multiplexer_8_out), .A(ID_EX_ra_2), .MOVbit(MOVbit_q), .MOV_WE(MOVSelector_mov_we),
    .Result(MOVSelector_result));
  and NO_MOV (NO_MOV_out, MOVSelector_mov_we, WE_q);
  MEM_WB EX_MEM (
    .MOVbit(MOVbit_q), .Result(MOVSelector_result), .ValB(multiplexer_6_out), .rd(ID_EX_rd_2),
    .OP(ID_EX_op_2), .R(R_q), .I(I_q), .WE(NO_MOV_out), .Clock(clock_1_out), .MOVbit_2(EX_MEM_movbit_2),
    .Result_2(EX_MEM_result_2), .ValB_2(EX_MEM_valb_2), .rd_2(EX_MEM_rd_2), .OP_2(EX_MEM_op_2),
    .R_2(EX_MEM_r_2), .I_2(EX_MEM_i_2), .WE_2(EX_MEM_we_2));  // open: Target, Target_2
  Register #(.width(32)) PC_2 (.D(ID_EX_pc_2), .Q(PC_2_q), .clk(clock_1_out));  // open: en, clr
  Register #(.width(32)) PC_3 (.D(PC_2_q), .clk(clock_1_out));  // open: en, Q, clr
  MEM_WB MEM_WB (
    .MOVbit(EX_MEM_movbit_2), .Result(EX_MEM_result_2), .ValB(EX_MEM_valb_2), .rd(EX_MEM_rd_2),
    .OP(EX_MEM_op_2), .R(EX_MEM_r_2), .I(EX_MEM_i_2), .WE(EX_MEM_we_2), .Clock(clock_1_out),
    .Result_2(registerfile_1_p1), .rd_2(registerfile_1_p4), .WE_2(registerfile_1_p3));  // open: Target, MOVbit_2, Target_2, ValB_2, OP_2, R_2, I_2
  // AND_Gate and_2 is placed but not wired

  // Notes on the sheet:
  //   b4-b0
  //   b2
  //   incomplete
endmodule

module PC_4 (
  input  [31:0] PCin,
  output [31:0] PC_4
);

  Adder #(.width(30)) adder_1 (.a(PCin[31:2]), .b(30'h1), .out(PC_4[31:2]));  // open: cin, cout

  assign PC_4[1:0] = PCin[1:0];
endmodule

module IF_ID_Pipeline_Register (
  input  [31:0] Instruction,
  input  [31:0] PC_4,
  input  Clock,
  output [31:0] Instruction_2,
  output [31:0] PC_4_2
);

  Register #(.width(32)) u_PC_4 (.D(PC_4), .Q(PC_4_2), .clk(Clock));  // open: en, clr
  Register #(.width(32)) u_Instruction (.D(Instruction), .Q(Instruction_2), .clk(Clock));  // open: en, clr
endmodule

module Ins_Type_Decoder (
  input  [31:0] Instruction,
  output R,
  output I,
  output J
);

  wire and_1_out, and_2_out, and_4_out, and_5_out, not_1_out, not_2_out, not_3_out, not_4_out, not_5_out,
       not_6_out, not_7_out, not_8_out, not_9_out, or_2_out, or_3_out;

  not not_1 (not_1_out, Instruction[31]);
  not not_2 (not_2_out, Instruction[30]);
  not not_3 (not_3_out, Instruction[29]);
  not not_4 (not_4_out, Instruction[28]);
  not not_5 (not_5_out, Instruction[27]);
  not not_6 (not_6_out, Instruction[26]);
  not not_7 (not_7_out, Instruction[30]);
  not not_8 (not_8_out, Instruction[27]);
  and and_1 (and_1_out, ~Instruction[0], Instruction[1], ~Instruction[2], Instruction[3], ~Instruction[4], Instruction[5]);  // AND_Gate
  and and_2 (and_2_out, Instruction[0], Instruction[1], ~Instruction[2], Instruction[3], ~Instruction[4], Instruction[5]);  // AND_Gate
  and and_3 (R, not_1_out, not_2_out, not_3_out, not_4_out, not_5_out, not_6_out);
  and and_4 (and_4_out, not_7_out, not_8_out, Instruction[26]);
  or or_1 (I, and_4_out, Instruction[28], Instruction[29], Instruction[31]);
  or or_2 (or_2_out, and_1_out, and_2_out);
  and and_5 (and_5_out, R, or_2_out);
  or or_3 (or_3_out, I, R);
  not not_9 (not_9_out, or_3_out);
  or or_4 (J, not_9_out, and_5_out);
endmodule

module ID_EX_Registers (
  input  [4:0] Shamt,
  input  [5:0] Op,
  input  [31:0] ra,
  input  [31:0] rb,
  input  [31:0] immediate,
  input  [4:0] rd,
  input  [3:0] ALUop,
  input  [31:0] PC,
  input  in_9,
  output [4:0] Shamt_2,
  output [5:0] Op_2,
  output [31:0] ra_2,
  output [31:0] rb_2,
  output [31:0] immediate_2,
  output [4:0] rd_2,
  output [3:0] ALUop_2,
  output [31:0] PC_2
);

  Register #(.width(5)) u_Shamt (.D(Shamt), .Q(Shamt_2), .clk(in_9));  // open: en, clr
  Register #(.width(6)) u_Op (.D(Op), .Q(Op_2), .clk(in_9));  // open: en, clr
  Register #(.width(32)) u_ra (.D(ra), .Q(ra_2), .clk(in_9));  // open: en, clr
  Register #(.width(32)) u_rb (.D(rb), .Q(rb_2), .clk(in_9));  // open: en, clr
  Register #(.width(32)) u_immediate (.D(immediate), .Q(immediate_2), .clk(in_9));  // open: en, clr
  Register #(.width(5)) u_rd (.D(rd), .Q(rd_2), .clk(in_9));  // open: en, clr
  Register #(.width(4)) u_ALUop (.D(ALUop), .Q(ALUop_2), .clk(in_9));  // open: en, clr
  Register #(.width(32)) PC_4 (.D(PC), .Q(PC_2), .clk(in_9));  // open: en, clr
endmodule

module I_Type_Decoder (
  input  [31:0] Instruction,
  output [15:0] immediate,
  output [4:0] rd,
  output [4:0] rs,
  output [5:0] op
);


  assign immediate = Instruction[15:0];
  assign op = Instruction[31:26];
  assign rd = Instruction[20:16];
  assign rs = Instruction[25:21];
endmodule

module R_Decoder (
  input  [31:0] Instruction,
  output [5:0] func,
  output [4:0] shamt,
  output [4:0] rd,
  output [4:0] rb,
  output [4:0] ra,
  output [5:0] op
);


  assign func = Instruction[5:0];
  assign op = Instruction[31:26];
  assign ra = Instruction[25:21];
  assign rb = Instruction[20:16];
  assign rd = Instruction[15:11];
  assign shamt = Instruction[10:6];
endmodule

// I ALUop decode
module I_Type_ALUOP_Decoder (
  input  [5:0] Op,
  output [3:0] out_2
);

  wire and_1_out, not_1_out, not_2_out, not_3_out, not_4_out;

  not not_1 (not_1_out, Op[1]);
  not not_2 (not_2_out, Op[0]);
  not not_3 (not_3_out, Op[1]);
  not not_4 (not_4_out, Op[0]);
  and and_1 (and_1_out, Op[2], not_1_out);
  and and_2 (out_2[2], Op[1], not_2_out);
  and and_3 (out_2[1], not_3_out, Op[0]);
  or or_1 (out_2[3], not_4_out, and_1_out);

  assign out_2[0] = 1'b0;
endmodule

module I_Everything (
  input  [31:0] in_1,
  output [31:0] immediate,
  output [4:0] rs,
  output [4:0] rd,
  output [3:0] ALUop,
  output useCOMPARATOR
);

  wire not_1_out, not_2_out, not_3_out;
  wire [5:0] Instruction_Splitter_op;
  wire [15:0] Instruction_Splitter_immediate;

  I_Type_Decoder Instruction_Splitter (
    .Instruction(in_1), .immediate(Instruction_Splitter_immediate), .rd(rs), .rs(rd),
    .op(Instruction_Splitter_op));
  I_Type_ALUOP_Decoder i_type_aluop_decoder_1 (.Op(Instruction_Splitter_op), .out_2(ALUop));
  I_Extender Bit_Extender (
    ._16_bit_immediate(Instruction_Splitter_immediate), .opcode(Instruction_Splitter_op),
    ._32_bit_immediate(immediate));
  not not_1 (not_1_out, Instruction_Splitter_op[5]);
  not not_2 (not_2_out, Instruction_Splitter_op[4]);
  not not_3 (not_3_out, Instruction_Splitter_op[2]);
  and and_1 (useCOMPARATOR, not_1_out, not_2_out, Instruction_Splitter_op[3], not_3_out, Instruction_Splitter_op[1]);
endmodule

module I_Extender (
  input  [15:0] _16_bit_immediate,
  input  [5:0] opcode,
  output [31:0] _32_bit_immediate
);

  wire and_1_out, not_1_out;
  wire [31:0] bit_extender_1_out, bit_extender_2_out;

  assign bit_extender_1_out = {{16{_16_bit_immediate[15]}}, _16_bit_immediate};  // Bit_Extender bit_extender_1
  assign bit_extender_2_out = {{16{1'b0}}, _16_bit_immediate};  // Bit_Extender bit_extender_2
  not not_1 (not_1_out, opcode[2]);
  and and_1 (and_1_out, opcode[0], not_1_out);
  Multiplexer #(.width(32)) multiplexer_1 (
    .in0(bit_extender_1_out), .in1(bit_extender_2_out), .out(_32_bit_immediate), .sel(and_1_out));  // open: en
endmodule

module R_Everything (
  input  [31:0] Instruction,
  output [5:0] Func,
  output movbit,
  output [3:0] ALUop,
  output USECOMPARATOR,
  output [4:0] shamt,
  output [4:0] rd,
  output [4:0] rb,
  output [4:0] ra,
  output [5:0] opcode
);

  R_Decoder R_Ins_Splitter (
    .Instruction(Instruction), .func(Func), .shamt(shamt), .rd(rd), .rb(rb), .ra(ra), .op(opcode));
  R_mov_detector r_mov_detector_1 (.func(Func), .MOVbit(movbit));
  R_Func_ALUop r_func_aluop_1 (.func(Func), .aluop(ALUop), .USECOMPARATOR(USECOMPARATOR));
endmodule

module R_Func_ALUop (
  input  [5:0] func,
  output [3:0] aluop,
  output USECOMPARATOR
);

  wire and_1_out, and_2_out, and_3_out, and_5_out, not_1_out, not_2_out, not_3_out, not_4_out;

  and and_1 (and_1_out, func[5], func[2]);
  not not_1 (not_1_out, func[3]);
  and and_2 (and_2_out, func[3], func[0]);
  and and_3 (and_3_out, func[5], func[0]);
  not not_2 (not_2_out, func[5]);
  or or_1 (aluop[3], func[3], and_1_out);
  and and_4 (aluop[2], not_1_out, func[1]);
  or or_2 (aluop[1], and_2_out, and_3_out);
  and and_5 (and_5_out, not_2_out, func[0]);
  or or_3 (aluop[0], and_5_out, func[3]);
  not not_3 (not_3_out, func[4]);
  not not_4 (not_4_out, func[2]);
  and and_6 (USECOMPARATOR, func[5], not_3_out, func[3], not_4_out, func[1]);
endmodule

module I_compataor (
  input  [5:0] opcode,
  output dontuseALU
);

  wire not_1_out, not_2_out, not_3_out;

  not not_1 (not_1_out, opcode[5]);
  not not_2 (not_2_out, opcode[4]);
  not not_3 (not_3_out, opcode[2]);
  and and_1 (dontuseALU, not_1_out, not_2_out, opcode[3], not_3_out, opcode[1]);
endmodule

module MEM_WB (
  input  MOVbit,
  input  [31:0] Target,
  input  [31:0] Result,
  input  [31:0] ValB,
  input  [4:0] rd,
  input  [5:0] OP,
  input  R,
  input  I,
  input  WE,
  input  Clock,
  output MOVbit_2,
  output [31:0] Target_2,
  output [31:0] Result_2,
  output [31:0] ValB_2,
  output [4:0] rd_2,
  output [5:0] OP_2,
  output R_2,
  output I_2,
  output WE_2
);

  Register #(.width(1)) register_1 (.D(MOVbit), .Q(MOVbit_2), .clk(Clock));  // open: en, clr
  Register #(.width(32)) register_2 (.D(Target), .Q(Target_2), .clk(Clock));  // open: en, clr
  Register #(.width(32)) register_3 (.D(Result), .Q(Result_2), .clk(Clock));  // open: en, clr
  Register #(.width(32)) register_4 (.D(ValB), .Q(ValB_2), .clk(Clock));  // open: en, clr
  Register #(.width(5)) register_5 (.D(rd), .Q(rd_2), .clk(Clock));  // open: en, clr
  Register #(.width(6)) register_6 (.D(OP), .Q(OP_2), .clk(Clock));  // open: en, clr
  Register #(.width(1)) register_7 (.D(R), .Q(R_2), .clk(Clock));  // open: en, clr
  Register #(.width(1)) register_8 (.D(I), .Q(I_2), .clk(Clock));  // open: en, clr
  Register #(.width(1)) register_9 (.D(WE), .Q(WE_2), .clk(Clock));  // open: en, clr
endmodule

module R_mov_detector (
  input  [5:0] func,
  output MOVbit
);

  wire MOVN_out, MOVZ_out;

  and MOVZ (MOVZ_out, ~func[0], func[1], ~func[2], func[3], ~func[4], ~func[5]);  // AND_Gate
  and MOVN (MOVN_out, func[0], func[1], ~func[2], func[3], ~func[4], ~func[5]);  // AND_Gate
  or or_1 (MOVbit, MOVZ_out, MOVN_out);
endmodule

module MOVSelector (
  input  MOVbit,
  input  [31:0] ALUResult,
  input  [31:0] A,
  output [31:0] Result,
  output MOV_WE
);

  wire and_1_out;

  Multiplexer #(.width(32), .enable("false")) multiplexer_1 (.in0(ALUResult), .in1(A), .out(Result), .sel(MOVbit));
  and and_1 (and_1_out, MOVbit, ALUResult[0]);
  Multiplexer #(.enable("false")) multiplexer_2 (.in0(1'b1), .in1(and_1_out), .out(MOV_WE), .sel(MOVbit));
endmodule

module Comparator (
  input  [31:0] A,
  input  [31:0] B,
  input  [3:0] aluOP,
  input  [5:0] OP,
  input  R,
  output [31:0] Result
);

  wire comparator_1_lt, comparator_2_lt, I_Detector_signed, multiplexer_1_out, multiplexer_2_out,
       R_Detector_signed;

  CompSignR R_Detector (.aluOP(aluOP), .Signed(R_Detector_signed));
  CompSignI I_Detector (.OP(OP), .Signed(I_Detector_signed));
  Multiplexer multiplexer_1 (
    .in0(R_Detector_signed), .in1(I_Detector_signed), .out(multiplexer_1_out), .sel(R));  // open: en
  Comparator_part #(.width(32)) comparator_1 (.a(A), .b(B), .lt(comparator_1_lt));  // open: gt, eq
  Comparator_part #(.width(32), .mode("unsigned")) comparator_2 (.a(A), .b(B), .lt(comparator_2_lt));  // open: gt, eq
  Multiplexer multiplexer_2 (
    .in0(comparator_1_lt), .in1(comparator_2_lt), .out(multiplexer_2_out), .sel(multiplexer_1_out));  // open: en
  assign Result = {{31{1'b0}}, multiplexer_2_out};  // Bit_Extender bit_extender_1
endmodule

module CompSignR (
  input  [3:0] aluOP,
  output Signed
);

  not not_1 (Signed, aluOP[1]);
endmodule

module CompSignI (
  input  [5:0] OP,
  output Signed
);

  not not_1 (Signed, OP[0]);
endmodule

module SHAMT_Decoder (
  input  [5:0] OpCode,
  input  [5:0] Func,
  input  [4:0] Shamt,
  input  [31:0] B,
  output [4:0] SHAMT_2
);

  wire IsLUI_islui, IsVAR_isvar;
  wire [4:0] multiplexer_1_out;

  LUI_Decoder IsLUI (.OP(OpCode), .IsLUI(IsLUI_islui));
  SLLV_SLL_decoder IsVAR (.OP(OpCode), .Func(Func), .IsVar(IsVAR_isvar));
  Multiplexer #(.width(5)) multiplexer_1 (
    .in0(Shamt), .in1(B[4:0]), .out(multiplexer_1_out), .sel(IsVAR_isvar));  // open: en
  Multiplexer #(.width(5)) multiplexer_2 (
    .in0(multiplexer_1_out), .in1(5'b10000), .out(SHAMT_2), .sel(IsLUI_islui));  // open: en
endmodule

module LUI_Decoder (
  input  [5:0] OP,
  output IsLUI
);

  wire not_1_out, not_2_out;

  not not_1 (not_1_out, OP[5]);
  not not_2 (not_2_out, OP[4]);
  and and_1 (IsLUI, not_1_out, not_2_out, OP[3], OP[2], OP[1], OP[0]);
endmodule

module SLLV_SLL_decoder (
  input  [5:0] OP,
  input  [5:0] Func,
  output IsVar
);

  wire and_1_out, and_2_out, and_3_out, not_1_out, not_2_out, not_3_out, not_4_out, not_5_out, not_6_out,
       not_7_out, not_8_out, or_1_out;

  and and_1 (and_1_out, OP[5], OP[4], OP[3], OP[2], OP[1], OP[0]);
  not not_1 (not_1_out, and_1_out);
  not not_2 (not_2_out, Func[5]);
  not not_3 (not_3_out, Func[4]);
  not not_4 (not_4_out, Func[3]);
  not not_5 (not_5_out, Func[0]);
  not not_6 (not_6_out, Func[5]);
  not not_7 (not_7_out, Func[4]);
  not not_8 (not_8_out, Func[3]);
  and and_2 (and_2_out, not_2_out, not_3_out, not_4_out, Func[2], not_5_out);
  and and_3 (and_3_out, not_6_out, not_7_out, not_8_out, Func[2], Func[1]);
  or or_1 (or_1_out, and_2_out, and_3_out);
  and and_4 (IsVar, not_1_out, or_1_out);
endmodule
